// Logisim project A4_Circuitos_Implementados.circ as structural Verilog: 15 circuits, main circuit main
module main (
);

  CODIFICADOR_BCD Codificador_BCD ();  // open: I0, I1, I2, I3, I4, I5, I6, I7, I8, I9, A3, A2, A1, A0
  MUX_8 MUX_8 ();  // open: S2, S1, S0, I0, I1, I2, I3, I4, I5, I6, I7, Y
  DECODIFICADOR_BCD Decodificador_BCD ();  // open: A3, A2, A1, A0, Y0, Y1, Y2, Y3, Y4, Y5, Y6, Y7, Y8, Y9
  DEMUX_8 DEMUX_8 ();  // open: E, S2, S1, S0, Y0, Y1, Y2, Y3, Y4, Y5, Y6, Y7
  MEIO_SOMADOR MEIO_SOMADOR ();  // open: A, B, S__Soma, C__Vai_um
  SOMADOR_COMPLETO_1BIT SOMADOR_COMPLETO_1BIT ();  // open: A, B, Cin, S__Soma, Cout
  SOMADOR_COMPLETO_4BIT SOMADOR_COMPLETO_4BIT ();  // open: A0, B0, Cin0, A1, B1, A2, B2, A3, B3, S0, S1, S2, S3, Cout_F
  CONTADOR_CRESCENTE_DECRESCENTE Contador_Crescente_Decrescente ();  // open: M, Q0, Q1, Q2, Q3
endmodule

module CODIFICADOR_BCD (
  input  I0,
  input  I1,
  input  I2,
  input  I3,
  input  I4,
  input  I5,
  input  I6,
  input  I7,
  input  I8,
  input  I9,
  output A3,
  output A2,
  output A1,
  output A0
);

  or or_1 (A3, I8, I9);
  or or_2 (A2, I4, I5, I6, I7);
  or or_3 (A1, I2, I3, I6, I7);
  or or_4 (A0, I1, I3, I5, I7, I9);
endmodule

module DECODIFICADOR_BCD (
  input  A3,
  input  A2,
  input  A1,
  input  A0,
  output Y0,
  output Y1,
  output Y2,
  output Y3,
  output Y4,
  output Y5,
  output Y6,
  output Y7,
  output Y8,
  output Y9
);

  wire not_1_out, not_2_out, not_3_out, not_4_out, not_5_out, not_6_out, not_7_out, not_8_out, not_9_out,
       not_10_out, not_11_out, not_12_out, not_13_out, not_14_out, not_15_out, not_16_out, not_17_out,
       not_18_out, not_19_out, not_20_out, not_21_out, not_22_out, not_23_out, not_24_out, not_25_out;

  not not_1 (not_1_out, A3);
  not not_2 (not_2_out, A2);
  not not_3 (not_3_out, A1);
  not not_4 (not_4_out, A0);
  not not_5 (not_5_out, A3);
  not not_6 (not_6_out, A2);
  not not_7 (not_7_out, A1);
  not not_8 (not_8_out, A3);
  not not_9 (not_9_out, A2);
  not not_10 (not_10_out, A0);
  not not_11 (not_11_out, A3);
  not not_12 (not_12_out, A2);
  not not_13 (not_13_out, A3);
  not not_14 (not_14_out, A1);
  not not_15 (not_15_out, A0);
  not not_16 (not_16_out, A3);
  not not_17 (not_17_out, A1);
  not not_18 (not_18_out, A3);
  not not_19 (not_19_out, A0);
  not not_20 (not_20_out, A3);
  not not_21 (not_21_out, A2);
  not not_22 (not_22_out, A1);
  not not_23 (not_23_out, A0);
  not not_24 (not_24_out, A2);
  not not_25 (not_25_out, A1);
  and and_1 (Y0, not_1_out, not_2_out, not_3_out, not_4_out);
  and and_2 (Y1, not_5_out, not_6_out, not_7_out, A0);
  and and_3 (Y2, not_8_out, not_9_out, A1, not_10_out);
  and and_4 (Y3, not_11_out, not_12_out, A1, A0);
  and and_5 (Y4, not_13_out, A2, not_14_out, not_15_out);
  and and_6 (Y5, not_16_out, A2, not_17_out, A0);
  and and_7 (Y6, not_18_out, A2, A1, not_19_out);
  and and_8 (Y7, not_20_out, A2, A1, A0);
  and and_9 (Y8, A3, not_21_out, not_22_out, not_23_out);
  and and_10 (Y9, A3, not_24_out, not_25_out, A0);
endmodule

module MUX_8 (
  input  S2,
  input  S1,
  input  S0,
  input  I0,
  input  I1,
  input  I2,
  input  I3,
  input  I4,
  input  I5,
  input  I6,
  input  I7,
  output Y
);

  wire and_1_out, and_2_out, and_3_out, and_4_out, and_5_out, and_6_out, and_7_out, and_8_out, not_1_out,
       not_2_out, not_3_out, not_4_out, not_5_out, not_6_out, not_7_out, not_8_out, not_9_out, not_10_out,
       not_11_out, not_12_out;

  not not_1 (not_1_out, S2);
  not not_2 (not_2_out, S1);
  not not_3 (not_3_out, S0);
  not not_4 (not_4_out, S2);
  not not_5 (not_5_out, S1);
  not not_6 (not_6_out, S2);
  not not_7 (not_7_out, S0);
  not not_8 (not_8_out, S2);
  not not_9 (not_9_out, S1);
  not not_10 (not_10_out, S0);
  not not_11 (not_11_out, S1);
  not not_12 (not_12_out, S0);
  and and_1 (and_1_out, not_1_out, not_2_out, not_3_out, I0);
  and and_2 (and_2_out, not_4_out, not_5_out, S0, I1);
  and and_3 (and_3_out, not_6_out, S1, not_7_out, I2);
  and and_4 (and_4_out, not_8_out, S1, S0, I3);
  and and_5 (and_5_out, S2, not_9_out, not_10_out, I4);
  and and_6 (and_6_out, S2, not_11_out, S0, I5);
  and and_7 (and_7_out, S2, S1, not_12_out, I6);
  and and_8 (and_8_out, S2, S1, S0, I7);
  or or_1 (Y, and_1_out, and_2_out, and_3_out, and_4_out, and_5_out, and_6_out, and_7_out, and_8_out);
endmodule

module DEMUX_8 (
  input  E,
  input  S2,
  input  S1,
  input  S0,
  output Y0,
  output Y1,
  output Y2,
  output Y3,
  output Y4,
  output Y5,
  output Y6,
  output Y7
);

  wire not_1_out, not_2_out, not_3_out, not_4_out, not_5_out, not_6_out, not_7_out, not_8_out, not_9_out,
       not_10_out, not_11_out, not_12_out;

  not not_1 (not_1_out, S2);
  not not_2 (not_2_out, S1);
  not not_3 (not_3_out, S0);
  not not_4 (not_4_out, S2);
  not not_5 (not_5_out, S1);
  not not_6 (not_6_out, S2);
  not not_7 (not_7_out, S0);
  not not_8 (not_8_out, S2);
  not not_9 (not_9_out, S1);
  not not_10 (not_10_out, S0);
  not not_11 (not_11_out, S1);
  not not_12 (not_12_out, S0);
  and and_1 (Y7, E, S2, S1, S0);
  and and_2 (Y0, E, not_1_out, not_2_out, not_3_out);
  and and_3 (Y1, E, not_4_out, not_5_out, S0);
  and and_4 (Y2, E, not_6_out, S1, not_7_out);
  and and_5 (Y3, E, not_8_out, S1, S0);
  and and_6 (Y4, E, S2, not_9_out, not_10_out);
  and and_7 (Y5, E, S2, not_11_out, S0);
  and and_8 (Y6, E, S2, S1, not_12_out);
endmodule

module MEIO_SOMADOR (
  input  A,
  input  B,
  output S__Soma,
  output C__Vai_um
);

  xor xor_1 (S__Soma, A, B);
  and and_1 (C__Vai_um, A, B);
endmodule

module SOMADOR_COMPLETO_1BIT (
  input  A,
  input  B,
  input  Cin,
  output S__Soma,
  output Cout
);

  wire and_1_out, and_2_out, xor_1_out;

  xor xor_1 (xor_1_out, A, B);
  xor xor_2 (S__Soma, xor_1_out, Cin);
  and and_1 (and_1_out, xor_1_out, Cin);
  and and_2 (and_2_out, A, B);
  or or_1 (Cout, and_1_out, and_2_out);
endmodule

module SOMADOR_COMPLETO_4BIT (
  input  A0,
  input  B0,
  input  Cin0,
  input  A1,
  input  B1,
  input  A2,
  input  B2,
  input  A3,
  input  B3,
  output S0,
  output S1,
  output S2,
  output S3,
  output Cout_F
);

  wire somador_completo_1bit_1_cout, somador_completo_1bit_2_cout, somador_completo_1bit_3_cout;

  SOMADOR_COMPLETO_1BIT somador_completo_1bit_1 (
    .A(A0), .B(B0), .Cin(Cin0), .S__Soma(S0), .Cout(somador_completo_1bit_1_cout));
  SOMADOR_COMPLETO_1BIT somador_completo_1bit_2 (
    .A(A1), .B(B1), .Cin(somador_completo_1bit_1_cout), .S__Soma(S1), .Cout(somador_completo_1bit_2_cout));
  SOMADOR_COMPLETO_1BIT somador_completo_1bit_3 (
    .A(A2), .B(B2), .Cin(somador_completo_1bit_2_cout), .S__Soma(S2), .Cout(somador_completo_1bit_3_cout));
  SOMADOR_COMPLETO_1BIT somador_completo_1bit_4 (
    .A(A3), .B(B3), .Cin(somador_completo_1bit_3_cout), .S__Soma(S3), .Cout(Cout_F));
endmodule

module CONTADOR_CRESCENTE_DECRESCENTE (
  input  M,
  output Q0,
  output Q1,
  output Q2,
  output Q3
);

  wire and_1_out, and_2_out, and_3_out, and_4_out, and_5_out, and_6_out, clock_1_out, FF0_qn, FF1_qn, FF2_qn,
       not_1_out, or_1_out, or_2_out, or_3_out;

  Clock clock_1 (.out(clock_1_out));
  not not_1 (not_1_out, M);
  J_K_Flip_Flop FF0 (.J(1'b1), .clk(clock_1_out), .K(1'b1), .Q(Q0), .Qn(FF0_qn));  // open: preset, en, reset
  and and_1 (and_1_out, M, Q0);
  and and_2 (and_2_out, not_1_out, FF0_qn);
  or or_1 (or_1_out, and_1_out, and_2_out);
  J_K_Flip_Flop FF1 (.J(or_1_out), .clk(clock_1_out), .K(or_1_out), .Q(Q1), .Qn(FF1_qn));  // open: preset, en, reset
  and and_3 (and_3_out, and_1_out, Q1);
  and and_4 (and_4_out, FF1_qn, and_2_out);
  or or_2 (or_2_out, and_3_out, and_4_out);
  J_K_Flip_Flop FF2 (.J(or_2_out), .clk(clock_1_out), .K(or_2_out), .Q(Q2), .Qn(FF2_qn));  // open: preset, en, reset
  and and_5 (and_5_out, and_3_out, Q2);
  and and_6 (and_6_out, FF2_qn, and_4_out);
  or or_3 (or_3_out, and_5_out, and_6_out);
  J_K_Flip_Flop FF3 (.J(or_3_out), .clk(clock_1_out), .K(or_3_out), .Q(Q3));  // open: Qn, preset, en, reset
endmodule

module SOMADOR_COMPLETO_1BIT_FORMA2 (
  input  A,
  input  B,
  input  Cin,
  output Cout,
  output Soma
);

  wire AB_out, ACin_out, BCin_out, m1_out, m2_out, m4_out, m7_out, not_1_out, not_2_out, not_3_out;

  not not_1 (not_1_out, A);
  not not_2 (not_2_out, B);
  not not_3 (not_3_out, Cin);
  and AB (AB_out, A, B);
  and ACin (ACin_out, A, Cin);
  and BCin (BCin_out, B, Cin);
  and m1 (m1_out, not_1_out, not_2_out, Cin);
  and m2 (m2_out, not_1_out, B, not_3_out);
  and m4 (m4_out, A, not_2_out, not_3_out);
  and m7 (m7_out, A, B, Cin);
  or or_1 (Cout, AB_out, ACin_out, BCin_out);
  or or_2 (Soma, m1_out, m2_out, m4_out, m7_out);

  // Notes on the sheet:
  //   Questao 2 - Forma 2: Somador Completo de 1 Bit (SOP / AND-OR)
endmodule

module COMPARADOR_3_BITS (
  input  A2,
  input  B2,
  input  A1,
  input  B1,
  input  A0,
  input  B0,
  output A____B__Igual
);

  wire A0____B0_out, A1____B1_out, A2____B2_out;

  xnor A2____B2 (A2____B2_out, A2, B2);
  xnor A1____B1 (A1____B1_out, A1, B1);
  xnor A0____B0 (A0____B0_out, A0, B0);
  and E (A____B__Igual, A2____B2_out, A1____B1_out, A0____B0_out);

  // Notes on the sheet:
  //   Questão 3: Comparador de 3 Bits (Saída = 1 se A2A1A0 == B2B1B0, senão 0)
endmodule

module DECODIFICADOR_7SEG (
  input  A__1,
  input  B__2,
  input  C__4,
  input  D__8,
  output a,
  output b,
  output c,
  output d,
  output e,
  output f,
  output g
);

  wire and_1_out, and_2_out, and_3_out, and_4_out, and_5_out, and_6_out, and_7_out, and_8_out, and_9_out,
       and_10_out, and_11_out, and_12_out, and_13_out, and_14_out, and_15_out, and_16_out, not_1_out,
       not_2_out, not_3_out;

  not not_1 (not_1_out, C__4);
  not not_2 (not_2_out, B__2);
  not not_3 (not_3_out, A__1);
  and and_1 (and_1_out, C__4, A__1);
  and and_2 (and_2_out, not_1_out, not_3_out);
  and and_3 (and_3_out, not_2_out, not_3_out);
  and and_4 (and_4_out, B__2, A__1);
  and and_5 (and_5_out, not_1_out, not_3_out);
  and and_6 (and_6_out, B__2, not_3_out);
  and and_7 (and_7_out, C__4, not_2_out, A__1);
  and and_8 (and_8_out, not_1_out, B__2);
  and and_9 (and_9_out, not_1_out, not_3_out);
  and and_10 (and_10_out, B__2, not_3_out);
  and and_11 (and_11_out, not_2_out, not_3_out);
  and and_12 (and_12_out, C__4, not_2_out);
  and and_13 (and_13_out, C__4, not_3_out);
  and and_14 (and_14_out, C__4, not_2_out);
  and and_15 (and_15_out, not_1_out, B__2);
  and and_16 (and_16_out, B__2, not_3_out);
  or or_1 (a, D__8, B__2, and_1_out, and_2_out);
  or or_2 (b, not_1_out, and_3_out, and_4_out);
  or or_3 (c, C__4, not_2_out, A__1);
  or or_4 (d, D__8, and_5_out, and_6_out, and_7_out, and_8_out);
  or or_5 (e, and_9_out, and_10_out);
  or or_6 (f, D__8, and_11_out, and_12_out, and_13_out);
  or or_7 (g, D__8, and_14_out, and_15_out, and_16_out);
  _7_Segment_Display u_7_segment_display_1 (.g(g), .f(f), .a(a), .b(b), .e(e), .d(d), .c(c));  // open: dp
endmodule

module BINARIO_PARA_GRAY (
  input  B3__MSB,
  input  B2,
  input  B1,
  input  B0__LSB,
  output G3__MSB,
  output G2,
  output G1,
  output G0__LSB
);

  xor xor_1 (G2, B3__MSB, B2);
  xor xor_2 (G1, B2, B1);
  xor xor_3 (G0__LSB, B1, B0__LSB);

  assign G3__MSB = B3__MSB;
endmodule

module GRAY_PARA_BINARIO (
  input  G3__MSB,
  input  G2,
  input  G1,
  input  G0__LSB,
  output B3__MSB,
  output B2,
  output B1,
  output B0__LSB
);

  xor xor_1 (B2, G3__MSB, G2);
  xor xor_2 (B1, B2, G1);
  xor xor_3 (B0__LSB, B1, G0__LSB);

  assign B3__MSB = G3__MSB;
endmodule

module MUX_MINTERMOS_0_2_4 (
  input  C__LSB,
  input  B,
  input  A__MSB,
  output S___F_A_B_C
);

  Multiplexer #(.select(3), .enable("false")) multiplexer_1 (
    .in0(1'b1), .in1(1'b0), .in2(1'b1), .in3(1'b0), .in4(1'b1), .in5(1'b0), .in6(1'b0), .in7(1'b0),
    .out(S___F_A_B_C), .sel({A__MSB, B, C__LSB}));
endmodule
