// Logisim project Circuitos_Modulo2_Logisim.circ as structural Verilog: 4 circuits, main circuit 1_Codificador_BCD
module _1_Codificador_BCD (
  input  I0,
  input  I1,
  input  I2,
  input  I3,
  input  I4,
  input  I5,
  input  I6,
  input  I7,
  input  I8,
  input  I9,
  output A3__8,
  output A2__4,
  output A1__2,
  output A0__1
);

  // OR_Gate A3_I8_I9 has open pins: out=A3__8
  or A2_I4_I5_I6_I7 (A2__4, I4, I5, I6, I7);
  or A1_I2_I3_I6_I7 (A1__2, I2, I3, I6, I7);
  or A0_I1_I3_I5_I7_I9 (A0__1, I1, I3, I5, I7, I9);

  // Notes on the sheet:
  //   1. CODIFICADOR BCD (Decimal I0..I9 para BCD A3 A2 A1 A0)
endmodule

// HA
module _5A_Meio_Somador (
  input  A,
  input  B,
  output Soma__S,
  output Carry__C
);

  xor XOR (Soma__S, A, B);
  and AND (Carry__C, A, B);

  // Notes on the sheet:
  //   5A. MEIO-SOMADOR (Half Adder: S = A xor B, C = A and B)
endmodule

// FA_1bit
module _5B_Somador_Completo_1bit (
  input  A,
  input  B,
  input  Cin,
  output S__Soma,
  output Cout
);

  wire AND1_out, AND2_out, XOR1_out;

  xor XOR1 (XOR1_out, A, B);
  xor XOR2 (S__Soma, XOR1_out, Cin);
  and AND1 (AND1_out, XOR1_out, Cin);
  and AND2 (AND2_out, A, B);
  or OR1 (Cout, AND1_out, AND2_out);

  // Notes on the sheet:
  //   5B. SOMADOR COMPLETO DE 1 BIT (Full Adder: 2 XOR, 2 AND, 1 OR)
endmodule

// FA_4bits
module _5C_Somador_Completo_4bits (
  input  A0,
  input  B0,
  input  Cin0,
  input  A1,
  input  B1,
  input  A2,
  input  B2,
  input  A3,
  input  B3,
  output S0,
  output S1,
  output S2,
  output S3,
  output Cout_Final
);

  wire AND1_0_out, AND1_1_out, AND1_2_out, AND1_3_out, AND2_0_out, AND2_1_out, AND2_2_out, AND2_3_out,
       OR1_0_out, OR1_1_out, OR1_2_out, XOR1_0_out, XOR1_1_out, XOR1_2_out, XOR1_3_out;

  xor XOR1_0 (XOR1_0_out, A0, B0);
  xor XOR1_1 (XOR1_1_out, A1, B1);
  xor XOR1_2 (XOR1_2_out, A2, B2);
  xor XOR1_3 (XOR1_3_out, A3, B3);
  xor XOR2_0 (S0, XOR1_0_out, Cin0);
  and AND1_0 (AND1_0_out, XOR1_0_out, Cin0);
  and AND2_0 (AND2_0_out, A0, B0);
  xor XOR2_1 (S1, XOR1_1_out, OR1_0_out);
  and AND1_1 (AND1_1_out, XOR1_1_out, OR1_0_out);
  and AND2_1 (AND2_1_out, A1, B1);
  xor XOR2_2 (S2, XOR1_2_out, OR1_1_out);
  and AND1_2 (AND1_2_out, XOR1_2_out, OR1_1_out);
  and AND2_2 (AND2_2_out, A2, B2);
  xor XOR2_3 (S3, XOR1_3_out, OR1_2_out);
  and AND1_3 (AND1_3_out, XOR1_3_out, OR1_2_out);
  and AND2_3 (AND2_3_out, A3, B3);
  or OR1_0 (OR1_0_out, AND1_0_out, AND2_0_out);
  or OR1_1 (OR1_1_out, AND1_1_out, AND2_1_out);
  or OR1_2 (OR1_2_out, AND1_2_out, AND2_2_out);
  or OR1_3 (Cout_Final, AND1_3_out, AND2_3_out);

  // Notes on the sheet:
  //   5C. SOMADOR COMPLETO DE 4 BITS (4 Andares: Cout de cima entra no Cin de baixo)
endmodule
